// Logisim project GLCPU.circ as structural Verilog: 5 circuits, main circuit main
module main (
);

  wire alu_1_c_out, alu_1_ovr, alu_1_zero;

  alu alu_1 (
    .ovr(alu_1_ovr), .c_out(alu_1_c_out), .zero(alu_1_zero));  // open: en, i3, i4, i5, c_in, r0, r1, r2, r3, r4, r5, r6, r7, s0, s1, s2, s3, s4, s5, s6, s7, f0, f1, f2, f3, f4, f5, f6, f7
  flags_register flags_register_1 (
    .ovrIn(alu_1_ovr), .cIn(alu_1_c_out), .zIn(alu_1_zero));  // open: store, clk, n_rst, overOut, cOut, zOut
endmodule

module alu (
  input  en,
  input  i3,
  input  i4,
  input  i5,
  input  c_in,
  input  r0,
  input  r1,
  input  r2,
  input  r3,
  input  r4,
  input  r5,
  input  r6,
  input  r7,
  input  s0,
  input  s1,
  input  s2,
  input  s3,
  input  s4,
  input  s5,
  input  s6,
  input  s7,
  output f0,
  output f1,
  output f2,
  output f3,
  output f4,
  output f5,
  output f6,
  output f7,
  output ovr,
  output c_out,
  output zero
);

  wire alu_op_select_op0, alu_op_select_op1, alu_op_select_op2, alu_op_select_op3, alu_op_select_op4,
       alu_slice0_c_out, alu_slice0_o, alu_slice1_c_out, alu_slice1_o, alu_slice2_c_out, alu_slice2_o,
       alu_slice3_c_out, alu_slice3_o, alu_slice4_c_out, alu_slice4_o, alu_slice5_c_out, alu_slice5_o,
       alu_slice6_c_out, alu_slice6_o, alu_slice7_o, and_1_out, and_3_out;

  alu_select alu_op_select (
    .i3(i3), .i4(i4), .i5(i5), .op0(alu_op_select_op0), .op1(alu_op_select_op1), .op2(alu_op_select_op2),
    .op3(alu_op_select_op3), .op4(alu_op_select_op4));
  alu_slice alu_slice0 (
    .op0(alu_op_select_op0), .op1(alu_op_select_op1), .op2(alu_op_select_op2), .op3(alu_op_select_op3),
    .op4(alu_op_select_op4), .r(r0), .s(s0), .c_in(c_in), .c_out(alu_slice0_c_out), .o(alu_slice0_o));
  alu_slice alu_slice1 (
    .op0(alu_op_select_op0), .op1(alu_op_select_op1), .op2(alu_op_select_op2), .op3(alu_op_select_op3),
    .op4(alu_op_select_op4), .r(r1), .s(s1), .c_in(alu_slice0_c_out), .c_out(alu_slice1_c_out),
    .o(alu_slice1_o));
  alu_slice alu_slice2 (
    .op0(alu_op_select_op0), .op1(alu_op_select_op1), .op2(alu_op_select_op2), .op3(alu_op_select_op3),
    .op4(alu_op_select_op4), .r(r2), .s(s2), .c_in(alu_slice1_c_out), .c_out(alu_slice2_c_out),
    .o(alu_slice2_o));
  alu_slice alu_slice3 (
    .op0(alu_op_select_op0), .op1(alu_op_select_op1), .op2(alu_op_select_op2), .op3(alu_op_select_op3),
    .op4(alu_op_select_op4), .r(r3), .s(s3), .c_in(alu_slice2_c_out), .c_out(alu_slice3_c_out),
    .o(alu_slice3_o));
  alu_slice alu_slice4 (
    .op0(alu_op_select_op0), .op1(alu_op_select_op1), .op2(alu_op_select_op2), .op3(alu_op_select_op3),
    .op4(alu_op_select_op4), .r(r4), .s(s4), .c_in(alu_slice3_c_out), .c_out(alu_slice4_c_out),
    .o(alu_slice4_o));
  alu_slice alu_slice5 (
    .op0(alu_op_select_op0), .op1(alu_op_select_op1), .op2(alu_op_select_op2), .op3(alu_op_select_op3),
    .op4(alu_op_select_op4), .r(r5), .s(s5), .c_in(alu_slice4_c_out), .c_out(alu_slice5_c_out),
    .o(alu_slice5_o));
  alu_slice alu_slice6 (
    .op0(alu_op_select_op0), .op1(alu_op_select_op1), .op2(alu_op_select_op2), .op3(alu_op_select_op3),
    .op4(alu_op_select_op4), .r(r6), .s(s6), .c_in(alu_slice5_c_out), .c_out(alu_slice6_c_out),
    .o(alu_slice6_o));
  alu_slice alu_slice7 (
    .op0(alu_op_select_op0), .op1(alu_op_select_op1), .op2(alu_op_select_op2), .op3(alu_op_select_op3),
    .op4(alu_op_select_op4), .r(r7), .s(s7), .c_in(alu_slice6_c_out), .c_out(c_out), .o(alu_slice7_o));
  xor xor_1 (ovr, alu_slice6_c_out, c_out);
  and and_1 (and_1_out, alu_slice7_o, alu_slice6_o, alu_slice5_o, alu_slice4_o);
  and and_2 (zero, and_1_out, and_3_out);
  and and_3 (and_3_out, alu_slice3_o, alu_slice2_o, alu_slice1_o, alu_slice0_o);
  assign f0 = en ? ~alu_slice0_o : 1'bz;  // Controlled_Inverter controlled_inverter_1
  assign f1 = en ? ~alu_slice1_o : 1'bz;  // Controlled_Inverter controlled_inverter_2
  assign f2 = en ? ~alu_slice2_o : 1'bz;  // Controlled_Inverter controlled_inverter_3
  assign f3 = en ? ~alu_slice3_o : 1'bz;  // Controlled_Inverter controlled_inverter_4
  assign f4 = en ? ~alu_slice4_o : 1'bz;  // Controlled_Inverter controlled_inverter_5
  assign f5 = en ? ~alu_slice5_o : 1'bz;  // Controlled_Inverter controlled_inverter_6
  assign f6 = en ? ~alu_slice6_o : 1'bz;  // Controlled_Inverter controlled_inverter_7
  assign f7 = en ? ~alu_slice7_o : 1'bz;  // Controlled_Inverter controlled_inverter_8
endmodule

module alu_select (
  input  i3,
  input  i4,
  input  i5,
  output op0,
  output op1,
  output op2,
  output op3,
  output op4
);

  wire nand_1_out, not_1_out;

  xor xor_1 (op0, i3, i5);
  xor xor_2 (op1, i4, i5);
  not not_1 (not_1_out, i5);
  nand nand_1 (nand_1_out, i3, i4, not_1_out);
  nand nand_2 (op2, nand_1_out, not_1_out);
  not not_2 (op3, nand_1_out);
  nor nor_1 (op4, not_1_out, i4);
endmodule

module alu_slice (
  input  op0,
  input  op1,
  input  op2,
  input  op3,
  input  op4,
  input  r,
  input  s,
  input  c_in,
  output c_out,
  output o
);

  wire nand_1_out, nand_2_out, nor_1_out, nor_2_out, nor_3_out, nor_4_out, not_1_out, xor_1_out, xor_2_out,
       xor_3_out;

  xor xor_1 (xor_1_out, op0, r);
  xor xor_2 (xor_2_out, op1, s);
  nand nand_1 (nand_1_out, xor_1_out, xor_2_out);
  nor nor_1 (nor_1_out, xor_1_out, xor_2_out);
  not not_1 (not_1_out, nor_1_out);
  nor nor_2 (nor_2_out, nand_1_out, op4);
  nor nor_3 (nor_3_out, nor_1_out, op3);
  nor nor_4 (nor_4_out, c_in, op2);
  nand nand_2 (nand_2_out, not_1_out, c_in);
  xor xor_3 (xor_3_out, nor_2_out, nor_3_out);
  nand nand_3 (c_out, nand_1_out, nand_2_out);
  xor xor_4 (o, xor_3_out, nor_4_out);
endmodule

module flags_register (
  input  ovrIn,
  input  cIn,
  input  zIn,
  input  store,
  input  clk,
  input  n_rst,
  output overOut,
  output cOut,
  output zOut
);

  wire not_1_out;

  not not_1 (not_1_out, n_rst);
  Register #(.width(1)) register_1 (.D(ovrIn), .en(store), .clk(clk), .Q(overOut), .clr(not_1_out));
  Register #(.width(1)) register_2 (.D(cIn), .en(store), .clk(clk), .Q(cOut), .clr(not_1_out));
  Register #(.width(1)) register_3 (.D(zIn), .en(store), .clk(clk), .Q(zOut), .clr(not_1_out));
endmodule
